// Logisim project SMA2.circ as structural Verilog: 2 circuits, main circuit main
module main (
  input  one,
  input  two,
  input  three,
  input  four,
  input  five
);

  wire and_1_out, clock_1_out, clock_edge_1_vout, clock_edge_2_vout, clock_edge_3_vout, clock_edge_4_vout,
       d_ff_1_q, d_ff_2_q, not_1_out, not_2_out, not_3_out, not_4_out, or_1_out;

  Clock clock_1 (.out(clock_1_out));
  clock_edge clock_edge_1 (.E(one), .clock(clock_1_out), .vOut(clock_edge_1_vout));
  clock_edge clock_edge_2 (.E(two), .clock(clock_1_out), .vOut(clock_edge_2_vout));
  clock_edge clock_edge_3 (.E(three), .clock(clock_1_out), .vOut(clock_edge_3_vout));
  clock_edge clock_edge_4 (.E(four), .clock(clock_1_out), .vOut(clock_edge_4_vout));
  clock_edge clock_edge_5 (.E(five), .clock(clock_1_out));  // open: vOut
  D_Flip_Flop d_ff_1 (.D(clock_edge_1_vout), .clk(clock_1_out), .Q(d_ff_1_q));  // open: Qn, preset, reset
  not not_1 (not_1_out, clock_edge_1_vout);
  or or_1 (or_1_out, d_ff_1_q, d_ff_2_q);
  not not_2 (not_2_out, clock_edge_2_vout);
  not not_3 (not_3_out, clock_edge_3_vout);
  not not_4 (not_4_out, clock_edge_4_vout);
  D_Flip_Flop d_ff_2 (.D(and_1_out), .clk(clock_1_out), .Q(d_ff_2_q));  // open: Qn, preset, reset
  and and_1 (and_1_out, not_2_out, not_3_out, not_1_out, not_4_out, or_1_out);
endmodule

module clock_edge (
  input  E,
  input  clock,
  output vOut
);

  wire and_1_out, and_2_out, and_3_out, and_4_out, or_1_out, or_2_out, or_3_out, Qa_q, Qb_q, Qb_qn;

  and and_1 (and_1_out, Qa_q, Qb_qn);
  and and_2 (and_2_out, E, Qb_q);
  D_Flip_Flop Qa (.D(or_1_out), .clk(clock), .Q(Qa_q));  // open: Qn, preset, reset
  or or_1 (or_1_out, and_1_out, and_2_out);
  or or_2 (or_2_out, E, Qa_q);
  and and_3 (and_3_out, or_2_out, Qb_qn);
  and and_4 (and_4_out, Qa_q, E);
  D_Flip_Flop Qb (.D(or_3_out), .clk(clock), .Q(Qb_q), .Qn(Qb_qn));  // open: preset, reset
  or or_3 (or_3_out, and_3_out, and_4_out);
  // Digital_Oscilloscope digital_oscilloscope_1: pin names not known; wires that end beside it: clock, E, Qa_q, Qb_q, vOut, 1'b1
  and and_5 (vOut, Qb_qn, Qa_q);
endmodule
